// Logisim project 10-0Boolean Algebra.circ as structural Verilog: 1 circuit, main circuit main
module main (
  input  A,
  input  A_2,
  input  B,
  input  C,
  output out_5,
  output out_6,
  output out_7,
  output out_8,
  output out_9,
  output out_10,
  output out_11,
  output out_12,
  output out_13,
  output out_14,
  output out_15,
  output out_16,
  output out_17,
  output out_18,
  output out_19,
  output out_20,
  output out_21,
  output out_22,
  output out_23,
  output out_24,
  output out_25,
  output out_26,
  output out_27,
  output out_28,
  output out_29,
  output out_30,
  output out_31,
  output out_32,
  output out_33
);

  wire and_1_out, and_2_out, and_4_out, and_5_out, and_7_out, and_8_out, and_9_out, and_11_out, and_14_out,
       not_1_out, not_2_out, not_3_out, not_4_out, not_5_out, not_6_out, not_7_out, not_8_out, or_1_out,
       or_2_out, or_3_out, or_4_out, or_6_out, or_7_out, or_8_out, or_9_out, or_10_out, or_14_out;

  not not_1 (not_1_out, A);
  not not_2 (not_2_out, A);
  not not_3 (not_3_out, A);
  // Probe on or_1_out
  or or_1 (or_1_out, A, 1'b0);
  or or_2 (or_2_out, A, 1'b1);
  // Probe on or_2_out
  and and_1 (and_1_out, A, 1'b0);
  // Probe on and_1_out
  and and_2 (and_2_out, A, 1'b1);
  // Probe on and_2_out
  // Probe on or_3_out
  or or_3 (or_3_out, A, A);
  // AND_Gate and_3 has open pins: in0=A, in1=A, out=open
  // Probe on or_4_out
  or or_4 (or_4_out, A, not_1_out);
  // Probe on and_4_out
  and and_4 (and_4_out, A, not_2_out);
  // Probe on not_4_out
  not not_4 (not_4_out, not_3_out);
  and and_5 (and_5_out, B, C);
  or or_5 (out_5, and_5_out, A_2);
  or or_6 (or_6_out, A_2, B);
  or or_7 (or_7_out, A_2, C);
  or or_8 (or_8_out, B, C);
  and and_6 (out_8, or_8_out, A_2);
  and and_7 (and_7_out, A_2, B);
  and and_8 (and_8_out, A_2, C);
  and and_9 (and_9_out, A_2, B);
  or or_9 (or_9_out, A_2, B);
  or or_10 (or_10_out, A_2, B);
  not not_5 (not_5_out, A_2);
  and and_10 (out_18, not_5_out, not_6_out);
  not not_6 (not_6_out, B);
  and and_11 (and_11_out, A_2, A_2);
  not not_7 (not_7_out, A_2);
  or or_11 (out_21, not_7_out, not_8_out);
  not not_8 (not_8_out, B);
  and and_12 (out_23, A_2, B);
  and and_13 (out_24, B, A_2);
  or or_12 (out_26, A_2, B);
  or or_13 (out_27, B, A_2);
  and and_14 (and_14_out, A_2, B);
  or or_14 (or_14_out, A_2, B);
  and and_15 (out_7, or_6_out, or_7_out);
  or or_15 (out_10, and_7_out, and_8_out);
  or or_16 (out_11, and_9_out, A_2);
  and and_16 (out_14, or_9_out, A_2);
  not not_9 (out_17, or_10_out);
  not not_10 (out_20, and_11_out);
  and and_17 (out_29, and_14_out, C);
  and and_18 (out_30, A_2, B, C);
  or or_17 (out_32, or_14_out, C);
  or or_18 (out_33, A_2, B, C);

  assign out_6 = A;
  assign out_9 = 1'b1;
  assign out_12 = 1'b0;
  assign out_13 = A_2;
  assign out_15 = A_2;
  assign out_16 = A;
  assign out_19 = A;
  assign out_22 = A;
  assign out_25 = 1'b1;
  assign out_28 = 1'b0;
  assign out_31 = A;

  // Notes on the sheet:
  //   Building Boolean Algebra
  //   A + 0 = A
  //   Union
  //   A + 1 = 1
  //   Intersection
  //   A * 0 = 0
  //   A * 1 = A
  //   Idempotent
  //   A + A = A
  //   A * A = A
  //   Complementary
  //   A + !A = 1
  //   A * !A = 0
  //   Double Negative
  //   !!A = A
  //   Distributive
  //   A + BC = (A+B)(A+C)
  //   A(B+C) = AB + AC
  //   Absorption
  //   A+ AB = A
  //   A * (A+B) = A
  //   DeMorgan's
  //   !(A+B) = !A * !B
  //   !(A*B) = !A + !B
  //   Commutative
  //   AB = BA
  //   A + B = B + A
  //   Associative
  //   A *  (B * C) = A * B * C
  //   A + (B + C) = A + B + C
endmodule
