// Logisim project 15_NAND and NOR Equivalence.circ as structural Verilog: 1 circuit, main circuit main
module main (
  input  A,
  input  B,
  input  A_2,
  input  B_2,
  output out_5,
  output out_6,
  output out_7,
  output out_8,
  output out_9,
  output out_10,
  output out_11,
  output out_12,
  output out_13,
  output out_14,
  output out_15,
  output out_16
);

  wire nand_1_out, nand_2_out, nand_3_out, nor_1_out, nor_2_out, nor_3_out;

  not not_1 (out_14, A_2);
  and and_1 (out_6, A_2, B_2);
  nand nand_1 (nand_1_out, A_2, B_2);
  or or_1 (out_10, A_2, B_2);
  nand nand_2 (nand_2_out, A_2, A_2);
  nand nand_3 (nand_3_out, B_2, B_2);
  nand nand_4 (out_16, B_2, B_2);
  nand nand_5 (out_7, nand_1_out, nand_1_out);
  nand nand_6 (out_11, nand_2_out, nand_3_out);
  not not_2 (out_13, A);
  and and_2 (out_5, A, B);
  nor nor_1 (nor_1_out, A, A);
  nor nor_2 (nor_2_out, B, B);
  or or_2 (out_9, A, B);
  nor nor_3 (nor_3_out, A, B);
  nor nor_4 (out_15, B, B);
  nor nor_5 (out_8, nor_1_out, nor_2_out);
  nor nor_6 (out_12, nor_3_out, nor_3_out);

  // Notes on the sheet:
  //   AND with NANDS
  //   OR with NANDS
  //   NOT with NANDS
  //   Use this space to build an AND gate out of NANDS
  //   AND with NORS
  //   Use this space to build an AND gate out of NORS
  //   OR with NORS
  //   NOT with NORS
endmodule
