// Logisim project 19_DflipflopBreakdown.circ as structural Verilog: 1 circuit, main circuit main
module main (
);

  wire and_1_out, and_2_out, and_3_out, and_4_out, and_5_out, and_6_out, Clk_out, d_ff_1_q, d_ff_1_qn,
       d_ff_2_q, d_ff_2_qn, d_ff_3_q, d_ff_3_qn, d_ff_4_q, d_ff_4_qn, nand_1_out, nand_2_out, nor_1_out,
       nor_2_out, not_2_out, not_3_out, not_4_out, or_1_out, or_2_out, or_3_out, or_4_out, or_5_out,
       or_6_out, or_7_out, or_8_out, or_9_out, or_10_out, or_11_out, or_12_out, or_13_out, xnor_1_out,
       xnor_2_out, xor_1_out;

  Clock Clk (.out(Clk_out));
  D_Flip_Flop d_ff_1 (
    .clk(Clk_out), .D(d_ff_1_qn), .Q(d_ff_1_q), .Qn(d_ff_1_qn), .preset(1'b0), .reset(1'b0));  // open: en
  // NOT_Gate not_1 has open pins: in=d_ff_4_q, out=open
  D_Flip_Flop d_ff_2 (
    .clk(d_ff_1_qn), .D(d_ff_2_qn), .Q(d_ff_2_q), .Qn(d_ff_2_qn), .preset(1'b0), .reset(1'b0));  // open: en
  not not_2 (not_2_out, d_ff_3_q);
  D_Flip_Flop d_ff_3 (
    .clk(d_ff_2_qn), .D(d_ff_3_qn), .Q(d_ff_3_q), .Qn(d_ff_3_qn), .preset(1'b0), .reset(1'b0));  // open: en
  not not_3 (not_3_out, d_ff_2_q);
  D_Flip_Flop d_ff_4 (
    .clk(d_ff_3_qn), .D(d_ff_4_qn), .Q(d_ff_4_q), .Qn(d_ff_4_qn), .preset(1'b0), .reset(1'b0));  // open: en
  not not_4 (not_4_out, d_ff_1_q);
  or or_1 (or_1_out, d_ff_2_q, d_ff_4_q);
  xnor xnor_1 (xnor_1_out, d_ff_3_q, d_ff_1_q);
  xnor xnor_2 (xnor_2_out, d_ff_2_q, d_ff_1_q);
  or or_2 (or_2_out, not_3_out, d_ff_1_q);
  nor nor_1 (nor_1_out, d_ff_3_q, d_ff_1_q);
  nand nand_1 (nand_1_out, d_ff_3_q, d_ff_1_q);
  or or_3 (or_3_out, not_2_out, d_ff_2_q);
  nor nor_2 (nor_2_out, d_ff_2_q, d_ff_1_q);
  or or_4 (or_4_out, or_1_out, xnor_1_out);
  or or_5 (or_5_out, not_2_out, xnor_2_out);
  or or_6 (or_6_out, or_2_out, d_ff_3_q);
  or or_7 (or_7_out, d_ff_4_q, nor_1_out);
  or or_8 (or_8_out, or_7_out, and_1_out);
  and and_1 (and_1_out, d_ff_2_q, nand_1_out);
  and and_2 (and_2_out, d_ff_3_q, and_3_out);
  and and_3 (and_3_out, not_3_out, d_ff_1_q);
  and and_4 (and_4_out, not_4_out, or_3_out);
  or or_9 (or_9_out, d_ff_4_q, nor_2_out);
  and and_5 (and_5_out, d_ff_3_q, nand_2_out);
  nand nand_2 (nand_2_out, d_ff_2_q, d_ff_1_q);
  or or_10 (or_10_out, d_ff_4_q, and_6_out);
  and and_6 (and_6_out, d_ff_2_q, not_4_out);
  or or_11 (or_11_out, or_8_out, and_2_out);
  or or_12 (or_12_out, or_9_out, and_5_out);
  or or_13 (or_13_out, or_10_out, xor_1_out);
  xor xor_1 (xor_1_out, d_ff_3_q, d_ff_2_q);
  _7_Segment_Display u_7_segment_display_1 (
    .g(or_13_out), .f(or_12_out), .a(or_4_out), .b(or_5_out), .e(and_4_out), .d(or_11_out), .c(or_6_out));  // open: dp

  // Notes on the sheet:
  //   c
  //   a
  //   b
  //   e
  //   d
  //   f
  //   g
endmodule
