// Logisim project 2016-10-03.circ as structural Verilog: 1 circuit, main circuit main
module main (
  input  P,
  input  T,
  input  V,
  input  S
);

  wire and_1_out, and_2_out, and_3_out, and_4_out, and_5_out, not_1_out, not_2_out, not_3_out, not_4_out,
       or_1_out, or_2_out, or_3_out;

  not not_1 (not_1_out, P);
  not not_2 (not_2_out, V);
  not not_3 (not_3_out, S);
  not not_4 (not_4_out, T);
  and and_1 (and_1_out, T, P);
  and and_2 (and_2_out, P, S);
  and and_3 (and_3_out, P, V);
  and and_4 (and_4_out, S, T);
  or or_1 (or_1_out, and_1_out, and_2_out);
  and and_5 (and_5_out, and_4_out, V);
  or or_2 (or_2_out, and_3_out, and_5_out);
  or or_3 (or_3_out, or_1_out, or_2_out);
  // Probe on or_3_out
endmodule
