// Logisim project 7 segment display with clock.circ as structural Verilog: 1 circuit, main circuit main
module main (
  input  A,
  input  B,
  input  C,
  input  D
);

  wire and_1_out, and_2_out, and_3_out, and_4_out, and_5_out, and_6_out, nand_1_out, nand_2_out, nor_1_out,
       nor_2_out, not_1_out, not_2_out, not_3_out, not_4_out, or_1_out, or_2_out, or_3_out, or_4_out,
       or_5_out, or_6_out, or_7_out, or_8_out, or_9_out, or_10_out, or_11_out, or_12_out, or_13_out,
       xnor_1_out, xnor_2_out, xor_1_out;

  not not_1 (not_1_out, A);
  not not_2 (not_2_out, B);
  not not_3 (not_3_out, C);
  not not_4 (not_4_out, D);
  or or_1 (or_1_out, not_3_out, D);
  nor nor_1 (nor_1_out, B, D);
  or or_2 (or_2_out, not_2_out, C);
  or or_3 (or_3_out, C, A);
  or or_4 (or_4_out, or_3_out, xnor_1_out);
  xnor xnor_1 (xnor_1_out, B, D);
  or or_5 (or_5_out, not_2_out, xnor_2_out);
  xnor xnor_2 (xnor_2_out, C, D);
  or or_6 (or_6_out, or_1_out, B);
  or or_7 (or_7_out, A, nor_1_out);
  and and_1 (and_1_out, C, nand_1_out);
  nand nand_1 (nand_1_out, B, D);
  and and_2 (and_2_out, not_3_out, D);
  and and_3 (and_3_out, not_4_out, or_2_out);
  or or_8 (or_8_out, A, nor_2_out);
  nor nor_2 (nor_2_out, C, D);
  nand nand_2 (nand_2_out, C, D);
  and and_4 (and_4_out, C, not_4_out);
  or or_9 (or_9_out, or_7_out, and_1_out);
  and and_5 (and_5_out, B, and_2_out);
  and and_6 (and_6_out, B, nand_2_out);
  or or_10 (or_10_out, A, and_4_out);
  xor xor_1 (xor_1_out, B, C);
  or or_11 (or_11_out, or_9_out, and_5_out);
  or or_12 (or_12_out, or_8_out, and_6_out);
  or or_13 (or_13_out, or_10_out, xor_1_out);
  _7_Segment_Display u_7_segment_display_1 (
    .g(or_13_out), .f(or_12_out), .a(or_4_out), .b(or_5_out), .e(and_3_out), .d(or_11_out), .c(or_6_out));  // open: dp

  // Notes on the sheet:
  //   a
  //   b
  //   c
  //   e
  //   f
  //   d
  //   g
endmodule
