// Logisim project birthday_problem2.circ as structural Verilog: 1 circuit, main circuit main
module main (
  input  A,
  input  B,
  input  C
);

  wire and_1_out, and_2_out, and_3_out, and_4_out, and_5_out, not_1_out, not_2_out, not_3_out, not_4_out,
       or_1_out;

  not not_1 (not_1_out, A);
  not not_2 (not_2_out, C);
  not not_3 (not_3_out, B);
  not not_4 (not_4_out, 1'b1);
  and and_1 (and_1_out, not_1_out, not_3_out);
  and and_2 (and_2_out, and_1_out, not_2_out);
  and and_3 (and_3_out, not_1_out, B);
  and and_4 (and_4_out, not_1_out, not_3_out);
  _7_Segment_Display #(.active("false")) u_7_segment_display_1 (
    .g(and_4_out), .f(or_1_out), .a(and_2_out), .b(not_4_out), .e(and_5_out), .d(and_2_out), .c(and_3_out));  // open: dp
  and and_5 (and_5_out, not_3_out, not_2_out);
  or or_1 (or_1_out, and_2_out, and_3_out);

  // Notes on the sheet:
  //   9 gates, 3 chips
endmodule
