// Logisim project birthday_problem_nandnor.circ as structural Verilog: 1 circuit, main circuit main
module main (
  input  A,
  input  B,
  input  C,
  input  A_2,
  input  B_2,
  input  C_2
);

  wire nand_1_out, nand_2_out, nand_3_out, nand_4_out, nand_5_out, nand_6_out, nand_7_out, nand_8_out,
       nand_9_out, nand_10_out, nand_11_out, nand_12_out, nand_13_out, nand_14_out, nand_15_out, nand_16_out,
       nor_1_out, nor_2_out, nor_3_out, nor_4_out, nor_5_out, nor_6_out, nor_7_out, nor_8_out, nor_9_out,
       nor_10_out, nor_11_out, nor_12_out;

  nand nand_1 (nand_1_out, A, A);
  nor nor_1 (nor_1_out, A_2, A_2);
  nand nand_2 (nand_2_out, B, B);
  nand nand_3 (nand_3_out, C, C);
  nor nor_2 (nor_2_out, B_2, B_2);
  nor nor_3 (nor_3_out, C_2, C_2);
  nand nand_4 (nand_4_out, nand_1_out, nand_2_out);
  nand nand_5 (nand_5_out, nand_1_out, B);
  nand nand_6 (nand_6_out, nand_1_out, nand_2_out);
  _7_Segment_Display #(.active("false")) u_7_segment_display_1 (
    .g(nand_10_out), .f(nand_16_out), .a(nand_13_out), .b(1'b0), .e(nand_11_out), .d(nand_13_out),
    .c(nand_9_out));  // open: dp
  nand nand_7 (nand_7_out, nand_2_out, nand_3_out);
  nor nor_4 (nor_4_out, B_2, B_2);
  nand nand_8 (nand_8_out, nand_4_out, nand_4_out);
  nand nand_9 (nand_9_out, nand_5_out, nand_5_out);
  nand nand_10 (nand_10_out, nand_6_out, nand_6_out);
  nand nand_11 (nand_11_out, nand_7_out, nand_7_out);
  nor nor_5 (nor_5_out, A_2, B_2);
  nor nor_6 (nor_6_out, A_2, nor_4_out);
  nor nor_7 (nor_7_out, A_2, B_2);
  nand nand_12 (nand_12_out, nand_8_out, nand_3_out);
  nand nand_13 (nand_13_out, nand_12_out, nand_12_out);
  nor nor_8 (nor_8_out, nor_5_out, nor_5_out);
  nor nor_9 (nor_9_out, nor_8_out, C_2);
  _7_Segment_Display #(.active("false")) u_7_segment_display_2 (
    .g(nor_7_out), .f(nor_12_out), .a(nor_9_out), .b(1'b0), .e(nor_10_out), .d(nor_9_out), .c(nor_6_out));  // open: dp
  nand nand_14 (nand_14_out, nand_13_out, nand_13_out);
  nand nand_15 (nand_15_out, nand_9_out, nand_9_out);
  nor nor_10 (nor_10_out, B_2, C_2);
  nand nand_16 (nand_16_out, nand_14_out, nand_15_out);
  nor nor_11 (nor_11_out, nor_9_out, nor_6_out);
  nor nor_12 (nor_12_out, nor_11_out, nor_11_out);

  // Notes on the sheet:
  //   16 gates, 4 chips
  //   12 gates, 3 chips
endmodule
